// Logisim project decoder_1035.circ as structural Verilog
module decoder_1035 (
  input  in_1,
  input  in_2,
  input  in_3,
  input  in_4,
  input  in_5,
  input  in_6,
  input  in_7,
  input  in_8,
  input  in_9,
  input  in_10,
  input  in_11,
  input  in_12,
  input  in_13,
  input  in_14,
  input  in_15,
  input  in_16,
  output out_17
);

  wire and_1_out, and_2_out, and_3_out, and_4_out, and_5_out, and_6_out, and_7_out, and_9_out, and_10_out,
       and_11_out, and_12_out, and_13_out, and_14_out, and_15_out, not_1_out, not_2_out, not_3_out,
       not_4_out, not_5_out, not_6_out, not_7_out, not_8_out, not_9_out, not_10_out, not_11_out, not_12_out;

  not not_1 (not_1_out, in_1);
  not not_2 (not_2_out, in_2);
  not not_3 (not_3_out, in_3);
  and and_1 (and_1_out, not_1_out, not_2_out);
  and and_2 (and_2_out, not_3_out, not_4_out);
  and and_3 (and_3_out, and_1_out, and_2_out);
  not not_4 (not_4_out, in_4);
  not not_5 (not_5_out, in_5);
  and and_4 (and_4_out, not_5_out, not_5_out, in_6);
  and and_5 (and_5_out, and_3_out, and_7_out);
  not not_6 (not_6_out, in_9);
  not not_7 (not_7_out, in_8);
  not not_8 (not_8_out, in_7);
  and and_6 (and_6_out, not_8_out, not_7_out);
  and and_7 (and_7_out, and_4_out, and_6_out);
  and and_8 (out_17, and_5_out, and_13_out);
  not not_9 (not_9_out, in_10);
  not not_10 (not_10_out, in_11);
  and and_9 (and_9_out, not_6_out, not_9_out);
  and and_10 (and_10_out, not_10_out, not_12_out);
  and and_11 (and_11_out, and_9_out, and_10_out);
  not not_11 (not_11_out, in_14);
  not not_12 (not_12_out, in_12);
  and and_12 (and_12_out, in_13, not_11_out);
  and and_13 (and_13_out, and_11_out, and_15_out);
  and and_14 (and_14_out, in_15, in_16);
  and and_15 (and_15_out, and_12_out, and_14_out);
endmodule
